# Fritzing sketch Pedestrian_Crossing_v1 (saved by Fritzing 0.9.9b)
circuit board: 8.46667cm x 5.64444cm
breadboards: 1

parts:
  Raspberry_Pi1 = Raspberry Pi 2
  R1 = Resistor [tolerance=±5% power=0.25 resistance=220 package=THT]
  R2 = Resistor [tolerance=±5% power=0.25 resistance=220 package=THT]
  LED1 = smd LED [color="Red (633nm)" package="0603 [SMD]"]
  LED2 = smd LED [color="Green (560nm)" package="0603 [SMD]"]
  S1 = Momentary Switch [package=ksa_sealed_tac_switch]

nets:
  N1: Raspberry_Pi1.GPIO2, LED2.cathode
  N2: Raspberry_Pi1.GPIO3, LED1.cathode
  N3: Raspberry_Pi1.GND, R1.Pin_1, R2.Pin_1, S1.2
  N4: Raspberry_Pi1.GPIO21, S1.4
  N5: R1.Pin_0, LED1.anode
  N6: R2.Pin_0, LED2.anode
